# Fritzing sketch NeoSectional_Schematic (saved by Fritzing 0.9.4)
circuit board: 10cm x 6cm
breadboards: 1

parts:
  J1 = Power Jack [package=power_jack_slot]
  IC1 = Voltage Regulator [package=78xxl]
  U1 = NodeMCU V1.0
  R1 = Resistor [tolerance=±5% resistance=10m package=THT]
  S1 = Toggle Switch [package=THT]
  R2 = Resistor [tolerance=±5% resistance=330 package=THT]
  NEOPIXEL1 = Neopixel Strip -- White (30/m)
  C2 = Electrolytic Capacitor [capacitance=10μF package="0605 [SMD, electrolytic]"]
  C1 = Electrolytic Capacitor [capacitance=1000μF package="1010 [SMD, electrolytic]"]

nets:
  GND: J1.GND, IC1.GND, U1.GND, R1.Pin_0, NEOPIXEL1.GND, C2.-, C1.-
  N1: J1.PWR, IC1.IN, C1.+
  VIN: IC1.OUT, U1.Vin, S1.L1, NEOPIXEL1.+5V, C2.+
  N2: U1.D1, R2.Pin_1
  N3: U1.D2, R1.Pin_1, S1.COM
  N4: R2.Pin_0, NEOPIXEL1.DO

custom parts:
  NodeMCU V1.0: ESP8266 based NodeMCU
  Neopixel Strip -- White (30/m): Neopixel Strip, White, 30 pixels per meter.
